// Logisim project Datapath_i2C.circ as structural Verilog: 1 circuit, main circuit main
module main (
  input  [7:0] in_1,
  input  in_2,
  input  in_3,
  input  in_4,
  input  in_5,
  input  in_6,
  input  in_7,
  input  [1:0] in_8,
  input  [1:0] in_9,
  input  in_10,
  input  in_11,
  input  in_12,
  output [7:0] out_13,
  output out_14,
  output out_15,
  output out_16,
  output out_17,
  output out_18,
  output out_19
);

  wire adder_1_out, bit2_cnt, clk, multiplexer_1_out, multiplexer_2_out, nor_1_out, not_1_out, not_2_out,
       not_3_out, not_4_out, reg_scl_ena_q, reg_scl_out_q, reg_sda_ena_q, reg_sda_in_q, reg_sda_out_q,
       shift_register_2_p16;
  wire [3:0] adder_2_out, bit16_cnt;

  Clock clock_1 (.out(clk));
  not not_1 (not_1_out, out_14);
  Register #(.width(1)) reg_sda_in (.D(out_14), .en(not_2_out), .clk(clk), .Q(reg_sda_in_q), .clr(in_12));
  not not_2 (not_2_out, in_10);
  not not_3 (not_3_out, bit2_cnt);
  and and_1 (out_16, not_1_out, not_2_out);
  Multiplexer #(.select(2), .enable("false")) multiplexer_1 (
    .in0(1'b1), .in1(not_3_out), .in2(bit2_cnt), .in3(bit16_cnt[0]), .out(multiplexer_1_out), .sel(in_9));
  not not_4 (not_4_out, in_1[0]);
  nor nor_1 (nor_1_out, not_4_out, in_2);
  // Shift_Register shift_register_1: pin names not known; wires that end beside it: in_12, in_3, bit16_cnt[0], clk, 1'b0, nor_1_out, in_1[1], in_1[2], in_1[3], in_1[4], in_1[5]
  Adder #(.width(1)) adder_1 (.a(bit2_cnt), .b(1'b1), .out(adder_1_out), .cin(1'b0), .cout(out_18));
  Adder #(.width(4)) adder_2 (.a(bit16_cnt), .b(4'b0001), .out(adder_2_out), .cin(1'b0), .cout(out_19));
  // Shift_Register shift_register_2: pin names not known; wires that end beside it: in_1[6], in_1[7], in_12, in_5, bit16_cnt[0], clk, 1'b0, reg_sda_in_q, 1'b0, 1'b0, 1'b0, 1'b0, 1'b0, 1'b0, 1'b0, shift_register_2_p16, out_13[0], out_13[1], out_13[2], out_13[3], out_13[4], out_13[5], out_13[6], out_13[7]
  Register #(.width(1)) rw_cnt (.D(in_1[0]), .en(in_4), .clk(clk), .Q(out_17), .clr(in_12));
  Register #(.width(1)) reg_scl_ena (.D(in_11), .en(1'b1), .clk(clk), .Q(reg_scl_ena_q), .clr(in_12));
  Register #(.width(1)) reg_scl_out (.D(multiplexer_1_out), .en(1'b1), .clk(clk), .Q(reg_scl_out_q), .clr(in_12));
  Register #(.width(1)) reg_cnt2 (.D(adder_1_out), .en(in_6), .clk(clk), .Q(bit2_cnt), .clr(in_12));
  Register #(.width(4)) reg_cnt16 (.D(adder_2_out), .en(in_7), .clk(clk), .Q(bit16_cnt), .clr(in_12));
  Multiplexer #(.select(2), .enable("false")) multiplexer_2 (
    .in0(1'b1), .in1(shift_register_2_p16), .in2(1'b0), .in3(1'b0), .out(multiplexer_2_out), .sel(in_8));
  assign out_15 = reg_scl_ena_q ? reg_scl_out_q : 1'bz;  // Controlled_Buffer controlled_buffer_1
  Register #(.width(1)) reg_sda_ena (.D(in_10), .en(1'b1), .clk(clk), .Q(reg_sda_ena_q), .clr(in_12));
  Register #(.width(1)) reg_sda_out (.D(multiplexer_2_out), .en(1'b1), .clk(clk), .Q(reg_sda_out_q), .clr(in_12));
  assign out_14 = reg_sda_ena_q ? reg_sda_out_q : 1'bz;  // Controlled_Buffer controlled_buffer_2

  // Other names for the same wires on the sheet: ack = out_16; bit_cnt2_ena = in_6; bit_cnt16_ena = in_7;
  //   cout2 = out_18; cout16 = out_19; load_mode = in_2; load_rw = in_4; load_val = in_3; read_val = in_5;
  //   reset = in_12; rw = out_17; SCL = out_15; scl_ena = in_11; scl_mode[1:0] = in_9; SDA = out_14; sda_ena = in_10;
  //   sda_mode[1:0] = in_8; val_rec[7:0] = out_13; VAL_SEND[7:0] = in_1

  // Notes on the sheet:
  //   data_bit_sig
  //   rw_sig
  //   mode_sig
  //   sda_sig
endmodule
