// Logisim project Datapath_I2C.circ as structural Verilog: 2 circuits, main circuit main
module main (
  input  [7:0] in_1,
  input  in_2,
  input  in_3,
  input  in_4,
  input  in_5,
  input  in_6,
  input  in_7,
  input  [1:0] in_8,
  input  [1:0] in_9,
  input  in_10,
  input  in_11,
  input  in_12,
  output [7:0] out_13,
  output out_14,
  output out_15,
  output out_16,
  output out_17,
  output out_18,
  output out_19
);

  wire adder_1_out, and_1_out, and_2_out, and_3_out, bit2_cnt_s, clk, multiplexer_1_out, multiplexer_2_out,
       nor_1_out, not_1_out, not_2_out, not_3_out, not_4_out, not_5_out, reg_scl_ena_q, reg_scl_out_q,
       reg_sda_ena_q, reg_sda_in_q, reg_sda_out_q, shift_register_2_p19, shift_register_2_p20;
  wire [3:0] adder_2_out, bit16_cnt_s;

  Clock clock_1 (.out(clk));
  and and_1 (and_1_out, bit16_cnt_s[0], not_1_out);
  not not_1 (not_1_out, in_5);
  and and_2 (and_2_out, bit16_cnt_s[0], in_5);
  not not_2 (not_2_out, in_1[0]);
  nor nor_1 (nor_1_out, not_2_out, in_3);
  Register #(.width(1)) rw_cnt (.D(in_1[0]), .en(in_3), .clk(clk), .Q(out_17), .clr(in_12));
  // Shift_Register shift_register_1: pin names not known; wires that end beside it: in_12, in_2, and_1_out, clk, 1'b0, nor_1_out, in_1[1], in_1[2]
  // Shift_Register shift_register_2: pin names not known; wires that end beside it: in_1[3], in_1[4], in_1[5], in_1[6], in_1[7], in_12, in_3, and_2_out, clk, 1'b0, in_1[0], in_1[1], in_1[2], in_1[3], in_1[4], in_1[5], in_1[6], in_1[7], shift_register_2_p19, shift_register_2_p20
  Adder #(.width(1)) adder_1 (.a(bit2_cnt_s), .b(1'b1), .out(adder_1_out), .cin(1'b0), .cout(out_18));
  Adder #(.width(4)) adder_2 (.a(bit16_cnt_s), .b(4'b0001), .out(adder_2_out), .cin(1'b0), .cout(out_19));
  Multiplexer #(.select(2), .enable("false")) multiplexer_1 (
    .in0(1'b1), .in1(shift_register_2_p19), .in2(shift_register_2_p20), .in3(1'b0), .out(multiplexer_1_out),
    .sel(in_8));
  Register #(.width(1)) reg_cnt2 (.D(adder_1_out), .en(in_6), .clk(clk), .Q(bit2_cnt_s), .clr(in_12));
  Register #(.width(4)) reg_cnt16 (.D(adder_2_out), .en(in_7), .clk(clk), .Q(bit16_cnt_s), .clr(in_12));
  Register #(.width(1)) reg_sda_ena (.D(in_10), .en(1'b1), .clk(clk), .Q(reg_sda_ena_q), .clr(in_12));
  Register #(.width(1)) reg_sda_out (.D(multiplexer_1_out), .en(1'b1), .clk(clk), .Q(reg_sda_out_q), .clr(in_12));
  assign out_14 = reg_sda_ena_q ? reg_sda_out_q : 1'bz;  // Controlled_Buffer controlled_buffer_1
  not not_3 (not_3_out, out_14);
  not not_4 (not_4_out, in_10);
  not not_5 (not_5_out, bit2_cnt_s);
  Register #(.width(1)) ack_reg (.D(and_3_out), .en(1'b1), .clk(clk), .Q(out_16), .clr(in_12));
  and and_3 (and_3_out, not_3_out, not_4_out);
  Register #(.width(1)) reg_sda_in (.D(out_14), .en(not_4_out), .clk(clk), .Q(reg_sda_in_q), .clr(in_12));
  Multiplexer #(.select(2), .enable("false")) multiplexer_2 (
    .in0(1'b1), .in1(not_5_out), .in2(bit2_cnt_s), .in3(bit16_cnt_s[0]), .out(multiplexer_2_out), .sel(in_9));
  // Shift_Register shift_register_3: pin names not known; wires that end beside it: in_12, in_4, bit16_cnt_s[0], clk, 1'b0, reg_sda_in_q, 1'b0, 1'b0, 1'b0, 1'b0, 1'b0, 1'b0, 1'b0, out_13[0], out_13[1], out_13[2], out_13[3], out_13[4], out_13[5], out_13[6], out_13[7]
  Register #(.width(1)) reg_scl_ena (.D(in_11), .en(1'b1), .clk(clk), .Q(reg_scl_ena_q), .clr(in_12));
  Register #(.width(1)) reg_scl_out (.D(multiplexer_2_out), .en(1'b1), .clk(clk), .Q(reg_scl_out_q), .clr(in_12));
  assign out_15 = reg_scl_ena_q ? reg_scl_out_q : 1'bz;  // Controlled_Buffer controlled_buffer_2

  // Other names for the same wires on the sheet: ack = out_16; bit_cnt2_ena = in_6; bit_cnt16_ena = in_7;
  //   cout2 = out_18; cout16 = out_19; load_add = in_3; load_val = in_2; read_val = in_4; reset = in_12; rw = out_17;
  //   SCL = out_15; scl_ena = in_11; scl_mode[1:0] = in_9; SDA = out_14; sda_ena = in_10; sda_mode[1:0] = in_8;
  //   shift_mode = in_5; VAL_REC[7:0] = out_13; VAL_SEND[7:0] = in_1

  // Notes on the sheet:
  //   not_shitft_mode_s
  //   shift_mode2_s
  //   shift_mode1_s
  //   lsb_s
  //   data_bit1_s
  //   data_bit2_s
  //   bit2_s
  //   bit16_s
  //   sda_pre_s
  //   sda_ena_s
  //   sda_s
  //   not_sda_ena_s
  //   not_bit2_cnt_s
  //   not_sda_s
  //   sda_bit_s
  //   scl_pre_s
  //   scl_ena_s
  //   scl_s
endmodule

module t (
  input  A,
  input  B,
  output Y,
  output Z
);

  wire not_1_out;

  not not_1 (not_1_out, B);
  and and_1 (Z, A, B);
  and and_2 (Y, A, not_1_out);
endmodule
